// Logisim project Lab3statemachine.circ as structural Verilog: 1 circuit, main circuit main
module main (
  input  [2:0] in_1,
  input  [1:0] in_2,
  output out_3
);

  wire clock_1_out;
  wire [2:0] register_1_q;
  wire [6:4] rom_1_data;

  Clock clock_1 (.out(clock_1_out));
  ROM #(.addrWidth(5), .dataWidth(7)) rom_1 (
    .addr({register_1_q, in_2}), .data({rom_1_data, out_3, in_1}), .sel(clock_1_out));
  Register #(.width(3)) register_1 (.D(rom_1_data), .Q(register_1_q));  // open: en, clk, clr

  // Notes on the sheet:
  //   contents of rom_1 (hex, n*v repeats v):
  //   0 10 20 8 10 20 30 9 20 30 40 a 30 40 8 b 40 8 9 c
endmodule
