// Logisim project lab2.circ as structural Verilog
module A____B (
  input  A1,
  input  A0,
  input  B1,
  input  B0,
  output AB
);

  wire and_1_out, and_2_out, and_3_out, and_4_out, and_5_out, not_1_out, not_2_out, not_3_out, not_4_out,
       not_5_out;

  not not_1 (not_1_out, A1);
  and and_1 (and_1_out, not_1_out, not_2_out);
  not not_2 (not_2_out, A0);
  not not_3 (not_3_out, A1);
  and and_2 (and_2_out, not_3_out, B0);
  not not_4 (not_4_out, A1);
  and and_3 (and_3_out, not_4_out, B1);
  not not_5 (not_5_out, A0);
  and and_4 (and_4_out, not_5_out, B1);
  and and_5 (and_5_out, B1, B0);
  or or_1 (AB, and_1_out, and_2_out, and_3_out, and_4_out, and_5_out);
endmodule

module A__B__8_1_MUX (
  input  A1,
  input  A0,
  input  B1,
  input  B0,
  output out_5
);

  Multiplexer #(.select(3), .enable("false")) multiplexer_1 (
    .in0(1'b1), .in1(1'b1), .in2(B0), .in3(1'b1), .in4(1'b0), .in5(1'b1), .in6(1'b0), .in7(B0), .out(out_5),
    .sel({A1, A0, B1}));
endmodule

module A__B__ROM (
  input  [1:0] A,
  input  [1:0] B,
  output out_3
);

  ROM #(.addrWidth(4), .dataWidth(1)) rom_1 (.addr({A, B}), .data(out_3));  // open: sel

  // Notes on the sheet:
  //   contents of rom_1 (hex, n*v repeats v):
  //   4*1 0 1 1 1 0 0 1 1 0 0 0 1
endmodule

module Minority_circuit (
  input  X,
  input  Y,
  input  Z,
  output Minority
);

  wire and_1_out, and_2_out, and_3_out, not_1_out, not_2_out, not_3_out, not_4_out, not_5_out, not_6_out;

  not not_1 (not_1_out, X);
  not not_2 (not_2_out, Y);
  not not_3 (not_3_out, X);
  not not_4 (not_4_out, Z);
  not not_5 (not_5_out, Y);
  not not_6 (not_6_out, Z);
  and and_1 (and_1_out, not_1_out, not_2_out);
  and and_2 (and_2_out, not_3_out, not_4_out);
  and and_3 (and_3_out, not_5_out, not_6_out);
  or or_1 (Minority, and_1_out, and_2_out, and_3_out);
endmodule

module Minority__8_1_MUX (
  input  X,
  input  Y,
  input  Z,
  output out_4
);

  Multiplexer #(.select(3), .enable("false")) multiplexer_1 (
    .in0(1'b1), .in1(1'b1), .in2(1'b1), .in3(1'b0), .in4(1'b1), .in5(1'b0), .in6(1'b0), .in7(1'b0),
    .out(out_4), .sel({X, Y, Z}));
endmodule

module Minority__ROM (
  input  [2:0] Z,
  output out_2
);

  ROM #(.addrWidth(3), .dataWidth(1)) rom_1 (.addr(Z), .data(out_2));  // open: sel

  // Notes on the sheet:
  //   X
  //   Y
  //   contents of rom_1 (hex, n*v repeats v):
  //   1 1 1 0 1
endmodule
